# Fritzing sketch schematic (saved by Fritzing 0.9.3b)
breadboards: 1

parts:
  U1 = ESP32S-HiLetgo [part_number=ESP32S-HiLetgo]
  S1 = Pushbutton [package="[THT]"]
  Q1 = NPN-Transistor [package="SOT-23 [SMD]"]
  LED1 = LED - 3mm [color="Red (633nm)" package="3 mm [THT]"]
  Part1 = Adafruit BMP180

nets:
  N1: U1.3.3, Part1.+3V3
  N2: U1.GPIO26, Q1.0
  N3: U1.GPIO12, S1.Pin_3, S1.Pin_4
  GND: U1.GND, U1.VIN, LED1.anode
  N4: S1.Pin_1, S1.Pin_2, Q1.2, Part1.GND
  N5: Q1.1, LED1.cathode

notes:
  Maybe protect IR LED with a resistor

custom parts:
  ESP32S-HiLetgo: HiLetgo ESP-WROOM-32 ESP32 ESP-32S Development Board 2.4GHz Dual-Mode WiFi + Bluetooth Dual Cores Microcontroller The ESP32 integrated with Antenna switches, RF Balun, power amplifiers, low-noise amplifiers, filters, and management modules, and the entire solution occupies the least area of PCB. 2.4 GHz Wi-Fi plus Bluetooth dual-mode chip, with TSMC Ultra-low power consumption 40nm technology,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
  Adafruit BMP180: This precision sensor from Bosch is the best low-cost sensing solution for measuring barometric pressure and temperature. Because pressure changes with altitude you can also use it as an altimeter! The sensor is soldered onto a PCB with a 3.3V regulator, I2C level shifter and pull-up resistors on the I2C pins. The BMP180 is the next-generation of sensors from Bosch, and replaces the BMP085.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
